# Fritzing sketch esp32_controller (saved by Fritzing 1.0.1rc)
circuit board: 11.6922cm x 8.11026cm
breadboards: 1

parts:
  ESP32 = DOIT Esp32 DevKit v1 (30 pins long, 11 pins width) [part_number=ESP32S-PIN30]
  Backward = SWITCH-MOMENTARY-2 [package=tactile-pth]
  Forward = SWITCH-MOMENTARY-2 [package=tactile-pth]
  Left = SWITCH-MOMENTARY-2 [package=tactile-pth]
  Right = SWITCH-MOMENTARY-2 [package=tactile-pth]
  Speed_Control = Rotary Potentiometer (Large) [maximum_resistance=100kΩ knob_status=50% package=THT]

nets:
  N1: ESP32.3V3, Speed_Control.leg1
  N2: ESP32.GND, Backward.2, Forward.2, Left.2, Right.2, Speed_Control.leg2
  N3: ESP32.D15, Left.1
  N4: ESP32.D18, Forward.1
  N5: ESP32.D19, Backward.1
  N6: ESP32.D21, Right.1
  N7: ESP32.D13, Speed_Control.wiper

notes:
  ESP32 Controller

custom parts:
  DOIT Esp32 DevKit v1 (30 pins long, 11 pins width): The DOIT Esp32 DevKit v1 is one of the development board created by DOIT to evaluate the ESP-WROOM-32 module. It is based on the ESP32 microcontroller that boasts Wifi, Bluetooth, Ethernet and Low Power support all in a single chip. (vanepp) made breadboard work, adjusted pin numbering and labels and reduced size of schematic and cleaned up pcb. This chip is 30pins long (2 x15) and 11 pins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
